// Logisim project Home_assignment_3.circ as structural Verilog: 2 circuits, main circuit main
module main (
  input  A1,
  input  B1,
  input  A2,
  input  B2,
  input  A3,
  input  B3,
  input  A4,
  input  B4,
  output Output1,
  output Output2,
  output Output3,
  output Output4,
  output Overflow
);

  wire and_1_out, and_2_out, and_3_out, and_4_out, and_5_out, and_6_out, and_7_out, or_1_out, or_2_out,
       xor_2_out, xor_3_out, xor_4_out;

  xor xor_1 (Output1, A1, B1);
  and and_1 (and_1_out, A1, A1);
  xor xor_2 (xor_2_out, A2, B2);
  and and_2 (and_2_out, A2, B2);
  xor xor_3 (xor_3_out, A3, B3);
  and and_3 (and_3_out, A3, B3);
  xor xor_4 (xor_4_out, A4, B4);
  and and_4 (and_4_out, A4, B4);
  and and_5 (and_5_out, and_1_out, xor_2_out);
  and and_6 (and_6_out, or_1_out, xor_3_out);
  and and_7 (and_7_out, or_2_out, xor_4_out);
  or or_1 (or_1_out, and_5_out, and_2_out);
  or or_2 (or_2_out, and_6_out, and_3_out);
  or or_3 (Overflow, and_7_out, and_4_out);
  xor xor_5 (Output2, xor_2_out, and_1_out);
  xor xor_6 (Output3, xor_3_out, or_1_out);
  xor xor_7 (Output4, xor_4_out, or_2_out);
endmodule

module FourBitFullAdder (
  input  A1,
  input  B1,
  input  A2,
  input  B2,
  input  A3,
  input  B3,
  input  A4,
  input  B4,
  output Output1,
  output Output2,
  output Output3,
  output Output4,
  output Overflow
);

  wire and_1_out, and_2_out, and_3_out, and_4_out, and_5_out, and_6_out, and_7_out, or_1_out, or_2_out,
       xor_2_out, xor_3_out, xor_4_out;

  xor xor_1 (Output1, A1, B1);
  and and_1 (and_1_out, A1, A1);
  xor xor_2 (xor_2_out, A2, B2);
  and and_2 (and_2_out, A2, B2);
  xor xor_3 (xor_3_out, A3, B3);
  and and_3 (and_3_out, A3, B3);
  xor xor_4 (xor_4_out, A4, B4);
  and and_4 (and_4_out, A4, B4);
  and and_5 (and_5_out, and_1_out, xor_2_out);
  and and_6 (and_6_out, or_1_out, xor_3_out);
  and and_7 (and_7_out, or_2_out, xor_4_out);
  or or_1 (or_1_out, and_5_out, and_2_out);
  or or_2 (or_2_out, and_6_out, and_3_out);
  or or_3 (Overflow, and_7_out, and_4_out);
  xor xor_5 (Output2, xor_2_out, and_1_out);
  xor xor_6 (Output3, xor_3_out, or_1_out);
  xor xor_7 (Output4, xor_4_out, or_2_out);
endmodule
