// Logisim project Home_assignment_4.circ as structural Verilog: 2 circuits, main circuit main
module main (
  input  in_1,
  input  in_2,
  input  in_3,
  input  in_4,
  input  A5,
  input  A1,
  input  A6,
  input  A2,
  input  in_9,
  input  A7,
  input  A3,
  input  A8,
  input  A4,
  input  in_14,
  input  B5,
  input  B1,
  input  B6,
  input  B2,
  input  B7,
  input  B3,
  input  B8,
  input  B4,
  output Ans
);

  wire adder_1_cout, adder_3_cout, and_1_out, and_2_out, and_3_out, and_4_out;
  wire [2:2] or_1_out;
  wire [3:0] adder_1_out, adder_2_out, adder_3_out, adder_4_out;

  Adder #(.width(4)) adder_1 (
    .a({A4, A3, A2, A1}), .b({B4, B3, B2, B1}), .out(adder_1_out), .cout(adder_1_cout));  // open: cin
  and and_1 (and_1_out, adder_1_out[2], adder_1_out[3]);
  and and_2 (and_2_out, adder_1_out[3], adder_1_out[1]);
  Adder #(.width(4)) adder_2 (
    .a({in_2, {2{or_1_out[2]}}, in_4}), .b(adder_1_out), .out(adder_2_out), .cin(in_14));  // open: cout
  or or_1 (or_1_out[2], and_1_out, adder_1_cout, and_2_out);
  Hex_Digit_Display hex_digit_display_1 (.value(adder_4_out));  // open: dp
  Adder #(.width(4)) adder_3 (
    .a({A8, A7, A6, A5}), .b({B8, B7, B6, B5}), .out(adder_3_out), .cin(or_1_out[2]), .cout(adder_3_cout));
  Hex_Digit_Display hex_digit_display_2 (.value(adder_2_out));  // open: dp
  and and_3 (and_3_out, adder_3_out[2], adder_3_out[3]);
  and and_4 (and_4_out, adder_3_out[3], adder_3_out[1]);
  Adder #(.width(4)) adder_4 (
    .a({in_1, {2{Ans}}, in_3}), .b(adder_3_out), .out(adder_4_out), .cin(in_9));  // open: cout
  or or_2 (Ans, and_3_out, adder_3_cout, and_4_out);
endmodule

module FourBitFullAdder (
  input  A1,
  input  B1,
  input  A2,
  input  B2,
  input  A3,
  input  B3,
  input  A4,
  input  B4,
  output Output1,
  output Output2,
  output Output3,
  output Output4,
  output Overflow
);

  wire and_1_out, and_2_out, and_3_out, and_4_out, and_5_out, and_6_out, and_7_out, or_1_out, or_2_out,
       xor_2_out, xor_3_out, xor_4_out;

  xor xor_1 (Output1, A1, B1);
  and and_1 (and_1_out, A1, A1);
  xor xor_2 (xor_2_out, A2, B2);
  and and_2 (and_2_out, A2, B2);
  xor xor_3 (xor_3_out, A3, B3);
  and and_3 (and_3_out, A3, B3);
  xor xor_4 (xor_4_out, A4, B4);
  and and_4 (and_4_out, A4, B4);
  and and_5 (and_5_out, and_1_out, xor_2_out);
  and and_6 (and_6_out, or_1_out, xor_3_out);
  and and_7 (and_7_out, or_2_out, xor_4_out);
  or or_1 (or_1_out, and_5_out, and_2_out);
  or or_2 (or_2_out, and_6_out, and_3_out);
  or or_3 (Overflow, and_7_out, and_4_out);
  xor xor_5 (Output2, xor_2_out, and_1_out);
  xor xor_6 (Output3, xor_3_out, or_1_out);
  xor xor_7 (Output4, xor_4_out, or_2_out);
endmodule
